# Fritzing sketch aansluitingultrasoon (saved by Fritzing 0.9.3b)
breadboards: 1

parts:
  ultrasoon_sensor = SRF05 Ultrasonic Rangefinder
  R1 = Resistor [tolerance=±5% resistance=1k package=THT]
  R2 = Resistor [tolerance=±5% resistance=1k package=THT]

nets:
  5V: ultrasoon_sensor.VCC
  GPIO 23 output: ultrasoon_sensor.Trig
  N1: ultrasoon_sensor.Echo, R1.Pin_0
  GND: ultrasoon_sensor.GND, R2.Pin_1
  GPIO 17 input: R1.Pin_1, R2.Pin_0
